// Logisim project LogisimMulticycleMIPS.circ as structural Verilog: 5 circuits, main circuit main
module main (
);

  wire ALUDecoder_itype, ALUDecoder_ldtype, ALUDecoder_rtype, ALUDecoder_sttype, ALUSelA, BType, clk,
       comparator_2_eq, comparator_3_eq, ExtOp, IRWr, JType, MemtoReg, MemWr, or_1_out, PCWr, RegDst,
       registerfile_1_p3, RegWr, Rst, TargetWr, Zero;
  wire [1:0] ALUSelB;
  wire [3:0] ALUCtr0, ALUCtr1, ALUOp, nstate, state;
  wire [4:0] multiplexer_1_out;
  wire [15:0] Imm16;
  wire [27:0] pc;
  wire [31:0] bit_extender_1_out, bit_extender_2_out, Imm32, mips_alu_1_p4, mips_ram_1_p6,
       mipsprogramrom_1_p2, multiplexer_3_out, multiplexer_4_out, multiplexer_7_out, npc, PCReg_q,
       registerfile_1_p1, registerfile_1_p7, registerfile_1_p8, shifter_1_out, TargetReg_q;
  wire [31:16] ins;
  wire [31:28] JumpPC;

  Register #(.width(4)) StateReg (.D(nstate), .en(1'b1), .clk(clk), .Q(state), .clr(Rst));
  Register #(.width(32)) PCReg (.D(npc), .en(PCWr), .clk(clk), .Q(PCReg_q), .clr(Rst));
  assign bit_extender_1_out = {{16{1'b0}}, Imm16};  // Bit_Extender bit_extender_1
  assign bit_extender_2_out = {{16{Imm16[15]}}, Imm16};  // Bit_Extender bit_extender_2
  Multiplexer #(.width(5), .enable("false")) multiplexer_1 (
    .in0(ins[20:16]), .in1(Imm16[15:11]), .out(multiplexer_1_out), .sel(RegDst));
  ALUControl ALUDecoder (
    .func3(Imm16[3]), .func2(Imm16[2]), .func1(Imm16[1]), .func0(Imm16[0]), .op5(ins[31]), .op4(ins[30]),
    .op3(ins[29]), .op2(ins[28]), .op1(ins[27]), .op0(ins[26]), .ALUctr3(ALUCtr1[3]), .ALUctr2(ALUCtr1[2]),
    .ALUctr1(ALUCtr1[1]), .ALUctr0(ALUCtr1[0]), .RType(ALUDecoder_rtype), .IType(ALUDecoder_itype),
    .BType(BType), .JType(JType), .LdType(ALUDecoder_ldtype), .StType(ALUDecoder_sttype));
  Multiplexer #(.width(32), .enable("false")) multiplexer_2 (
    .in0(bit_extender_1_out), .in1(bit_extender_2_out), .out(Imm32), .sel(ExtOp));
  // RegisterFile registerfile_1: pin names not known; wires that end beside it: registerfile_1_p1, clk, registerfile_1_p3, multiplexer_1_out, ins[25:21], ins[20:16], registerfile_1_p7, registerfile_1_p8
  Shifter #(.width(32)) shifter_1 (.in(Imm32), .\dist (5'b00010), .out(shifter_1_out));
  Multiplexer #(.width(32), .enable("false")) multiplexer_3 (
    .in0({JumpPC, pc}), .in1(registerfile_1_p7), .out(multiplexer_3_out), .sel(ALUSelA));
  Multiplexer #(.select(2), .width(32), .enable("false")) multiplexer_4 (
    .in0(32'h4), .in1(registerfile_1_p8), .in2(shifter_1_out), .in3(Imm32), .out(multiplexer_4_out),
    .sel(ALUSelB));
  Clock clock_1 (.out(clk));
  Button ResetButton (.out(Rst));
  NextState StateMachine (
    .state3(state[0]), .state2(state[1]), .state1(state[2]), .state0(state[3]), .RType(ALUDecoder_rtype),
    .IType(ALUDecoder_itype), .BType(BType), .JType(JType), .LdType(ALUDecoder_ldtype),
    .StType(ALUDecoder_sttype), .ALUOp3(ALUCtr0[3]), .ALUop2(ALUCtr0[2]), .ALUop1(ALUCtr0[1]),
    .ALUop0(ALUCtr0[0]), .ALUSelA(ALUSelA), .ALUSelB1(ALUSelB[1]), .ALUSelB0(ALUSelB[0]),
    .nstate3(nstate[3]), .nstate2(nstate[2]), .nstate1(nstate[1]), .nstate0(nstate[0]));
  // Mips_ALU mips_alu_1: pin names not known; wires that end beside it: multiplexer_3_out, multiplexer_4_out, ALUOp, mips_alu_1_p4, {32{1'b0}}
  Comparator #(.width(32), .mode("unsigned")) comparator_1 (
    .a({32{1'b0}}), .b(mips_alu_1_p4), .eq(Zero));  // open: gt, lt
  Comparator #(.width(4)) comparator_2 (.a(state), .b(4'b0010), .eq(comparator_2_eq));  // open: gt, lt
  Comparator #(.width(4)) comparator_3 (.a(state), .b(4'b0100), .eq(comparator_3_eq));  // open: gt, lt
  or or_1 (or_1_out, comparator_2_eq, comparator_3_eq);
  // MIPSProgramROM mipsprogramrom_1: pin names not known; wires that end beside it: PCReg_q, mipsprogramrom_1_p2
  Register #(.width(32)) TargetReg (.D(mips_alu_1_p4), .en(TargetWr), .clk(clk), .Q(TargetReg_q), .clr(Rst));
  // MIPS_RAM #(.addrWidth(24)) mips_ram_1: pin names not known; wires that end beside it: mips_alu_1_p4[25:2], registerfile_1_p8, MemWr, clk, MemtoReg, mips_ram_1_p6
  Register #(.width(32)) InstructionReg (.D(mipsprogramrom_1_p2), .en(IRWr), .clk(clk), .Q({ins, Imm16}), .clr(Rst));
  Multiplexer #(.width(32), .enable("false")) multiplexer_5 (
    .in0(mips_alu_1_p4), .in1(mips_ram_1_p6), .out(registerfile_1_p1), .sel(MemtoReg));
  Multiplexer #(.width(4), .enable("false")) multiplexer_6 (.in0(ALUCtr0), .in1(ALUCtr1), .out(ALUOp), .sel(or_1_out));
  RegWrControl RegWrSignal (
    .state3(state[3]), .state2(state[2]), .state1(state[1]), .state0(state[0]), .IRWr(IRWr), .PCWr(PCWr),
    .TargetWr(TargetWr), .RegWr(RegWr), .MemWr(MemWr));
  Multiplexer #(.width(32), .enable("false")) multiplexer_7 (
    .in0(mips_alu_1_p4), .in1(TargetReg_q), .out(multiplexer_7_out), .sel(BType));
  Multiplexer #(.width(32), .enable("false")) multiplexer_8 (
    .in0(multiplexer_7_out), .in1({JumpPC, ins[25:16], Imm16, 2'b00}), .out(npc), .sel(JType));

  // Other names for the same wires on the sheet: ins[15:0] = Imm16; JumpPC[27:2] = {ins[25:16], Imm16};
  //   Rd[4:0] = Imm16[15:11]; Rt[4:0] = ins[20:16]; Rs[4:0] = ins[25:21]; pc[31:28] = JumpPC

  // Notes on the sheet:
  //   Fetch
  //   Decode
  //   Execute&Memory&WB
  //   PC
  //   Not Mininum Hardware: Two memory and an adder
  //   Simulation controll pannel
  //   Instruction Memory
  //   contents of mipsprogramrom_1 (hex, n*v repeats v):
  //   loop: addiu $t5,$zero,9 addiu $t6,$zero,9 addu $t7,$t5,$t6 subu $t8,$t5,$t6
  //   #以上测试了addu,addiu,subu指令 addiu $s0,$zero,0   #将地址为最开始的基址放入$s0 addiu $t1,$zero,10 addiu $t2,$zero,0
  //   addiu $t3,$zero,100 ori $t2,$t2,1       #测试ori指令 beq $zero,$zero,condition  #测试beq指令 addiu
  //   $t5,$zero,0 j ocondition         condition: sw $t2,0($s0)    #测试sw指令 lw $t3,0($s0)    #测试lw指令
  //   ocondition: addiu $t4,$zero,9 subu $t1,$t1,$t4 sw $t1,4($s0) lw $t4,4($s0) j loop
  //   #测试Jump指令，之后会一直循环执行
  //   状态机在RExec或IExec时选择ALUDecoder输出的ALU操作码
endmodule

module RegWrControl (
  input  state3,
  input  state2,
  input  state1,
  input  state0,
  output IRWr,
  output PCWr,
  output TargetWr,
  output RegWr,
  output MemWr
);

  wire and_2_out, and_3_out, and_4_out, and_5_out, and_6_out, not_1_out, not_2_out, not_3_out, not_4_out,
       not_5_out, not_6_out, not_7_out, not_8_out, not_9_out, not_10_out, not_11_out, not_12_out, not_13_out,
       not_14_out, not_15_out, not_16_out;

  not not_1 (not_1_out, state3);
  and and_1 (IRWr, not_1_out, not_2_out, not_3_out);
  not not_2 (not_2_out, state1);
  not not_3 (not_3_out, state0);
  not not_4 (not_4_out, state3);
  not not_5 (not_5_out, state2);
  not not_6 (not_6_out, state1);
  not not_7 (not_7_out, state0);
  not not_8 (not_8_out, state3);
  not not_9 (not_9_out, state0);
  not not_10 (not_10_out, state3);
  not not_11 (not_11_out, state2);
  not not_12 (not_12_out, state3);
  not not_13 (not_13_out, state1);
  not not_14 (not_14_out, state2);
  not not_15 (not_15_out, state0);
  not not_16 (not_16_out, state2);
  and and_2 (and_2_out, not_4_out, not_5_out, not_6_out, not_7_out);
  or or_1 (PCWr, and_2_out, and_3_out);
  and and_3 (and_3_out, not_8_out, state2, state1, not_9_out);
  and and_4 (and_4_out, not_10_out, not_11_out, state1, state0);
  or or_2 (RegWr, and_4_out, and_5_out, and_6_out);
  and and_5 (and_5_out, not_12_out, state2, not_13_out, state0);
  and and_6 (and_6_out, state3, not_14_out, state1, not_15_out);
  and and_7 (MemWr, state3, not_16_out, state1, state0);

  assign TargetWr = 1'b0;
endmodule

module ALUControl (
  input  func3,
  input  func2,
  input  func1,
  input  func0,
  input  op5,
  input  op4,
  input  op3,
  input  op2,
  input  op1,
  input  op0,
  output ALUctr3,
  output ALUctr2,
  output ALUctr1,
  output ALUctr0,
  output RType,
  output IType,
  output BType,
  output JType,
  output LdType,
  output StType
);

  wire not_1_out, not_2_out;

  not not_1 (not_1_out, func3);
  not not_2 (not_2_out, func2);
  and and_1 (ALUctr0, not_1_out, not_2_out, func0);

  assign ALUctr1 = 1'b1;
  assign ALUctr2 = func1;
  assign ALUctr3 = 1'b0;
  assign BType = 1'b0;
  assign IType = 1'b0;
  assign JType = 1'b0;
  assign LdType = 1'b0;
  assign RType = 1'b1;
  assign StType = 1'b0;
endmodule

module NextState (
  input  state3,
  input  state2,
  input  state1,
  input  state0,
  input  RType,
  input  IType,
  input  BType,
  input  JType,
  input  LdType,
  input  StType,
  output ALUOp3,
  output ALUop2,
  output ALUop1,
  output ALUop0,
  output ALUSelA,
  output ALUSelB1,
  output ALUSelB0,
  output nstate3,
  output nstate2,
  output nstate1,
  output nstate0
);

  wire not_1_out, not_2_out, not_3_out;

  not not_1 (not_1_out, RType);
  or or_1 (ALUSelB1, state0, state1);
  not not_2 (not_2_out, state1);
  not not_3 (not_3_out, state0);
  and and_1 (ALUOp3, state0, not_1_out);
  and and_2 (nstate0, not_2_out, not_3_out);

  assign ALUop0 = state1;
  assign ALUop1 = 1'b1;
  assign ALUop2 = state1;
  assign ALUSelA = state0;
  assign ALUSelB0 = 1'b0;
  assign nstate1 = state0;
  assign nstate2 = 1'b0;
  assign nstate3 = 1'b0;
endmodule

module StateCoding (
);


  // Notes on the sheet:
  //   LWmem:1001
  //   LWwr:1010
  //   AddrCal:1000
  //   SWmem:1011
  //   Fetch:0000
  //   Decode:0001
  //   Rexec:0010
  //   Rfinish:0011
  //   Iexec:0100
  //   Ifinish:0101
  //   BrComplete: 0110
endmodule
