// Logisim project LogisimSinglecycleMIPS.circ as structural Verilog: 3 circuits, main circuit main
module main (
);

  wire ALUop0, ALUop1, ALUop2, ALUSrc, clk, ExtOp, Jump, MemtoReg, MemWr, nPC_sel, RegDst, registerfile_1_p7,
       RegWr, Rst, Zero;
  wire [3:0] ALUctr;
  wire [4:0] multiplexer_1_out;
  wire [15:0] Imm16;
  wire [27:0] pc;
  wire [31:0] adder_1_out, adder_2_out, bit_extender_1_out, bit_extender_2_out, datain, Imm32, mips_alu_1_p4,
       mips_ram_1_p6, multiplexer_3_out, multiplexer_4_out, multiplexer_5_out, npc, registerfile_1_p1,
       shifter_1_out;
  wire [31:16] ins;
  wire [31:28] JumpPC;

  Adder #(.width(32)) adder_1 (.a({JumpPC, pc}), .b(32'h4), .out(adder_1_out));  // open: cin, cout
  Shifter #(.width(32)) shifter_1 (.in(Imm32), .\dist (5'b00010), .out(shifter_1_out));
  assign bit_extender_1_out = {{16{1'b0}}, Imm16};  // Bit_Extender bit_extender_1
  assign bit_extender_2_out = {{16{Imm16[15]}}, Imm16};  // Bit_Extender bit_extender_2
  Multiplexer #(.width(5), .enable("false")) multiplexer_1 (
    .in0(ins[20:16]), .in1(Imm16[15:11]), .out(multiplexer_1_out), .sel(RegDst));
  Adder #(.width(32)) adder_2 (.a(adder_1_out), .b(shifter_1_out), .out(adder_2_out));  // open: cin, cout
  Multiplexer #(.width(32), .enable("false")) multiplexer_2 (
    .in0(bit_extender_1_out), .in1(bit_extender_2_out), .out(Imm32), .sel(ExtOp));
  // RegisterFile registerfile_1: pin names not known; wires that end beside it: registerfile_1_p1, clk, RegWr, multiplexer_1_out, ins[25:21], ins[20:16], registerfile_1_p7, datain
  Register #(.width(32)) register_1 (.D(npc), .en(1'b1), .clk(clk), .Q({JumpPC, pc}), .clr(Rst));
  Multiplexer #(.width(32), .enable("false")) multiplexer_3 (
    .in0(datain), .in1(Imm32), .out(multiplexer_3_out), .sel(ALUSrc));
  ALUControl alucontrol_1 (
    .ALUop2(ALUop2), .ALUop1(ALUop1), .ALUop0(ALUop0), .func3(Imm16[3]), .func2(Imm16[2]), .func1(Imm16[1]),
    .func0(Imm16[0]), .ALUctr3(ALUctr[3]), .ALUctr2(ALUctr[2]), .ALUctr1(ALUctr[1]), .ALUctr0(ALUctr[0]));
  Multiplexer #(.width(32), .enable("false")) multiplexer_4 (
    .in0(adder_1_out), .in1(adder_2_out), .out(multiplexer_4_out), .sel(Zero));
  // Mips_ALU mips_alu_1: pin names not known; wires that end beside it: registerfile_1_p7, multiplexer_3_out, ALUctr, mips_alu_1_p4, {32{1'b0}}
  Multiplexer #(.width(32), .enable("false")) multiplexer_5 (
    .in0(adder_1_out), .in1(multiplexer_4_out), .out(multiplexer_5_out), .sel(nPC_sel));
  Comparator #(.width(32), .mode("unsigned")) comparator_1 (
    .a({32{1'b0}}), .b(mips_alu_1_p4), .eq(Zero));  // open: gt, lt
  Clock clock_1 (.out(clk));
  Button ResetButton (.out(Rst));
  // MIPS_RAM #(.addrWidth(24)) mips_ram_1: pin names not known; wires that end beside it: mips_alu_1_p4[25:2], datain, MemWr, clk, MemtoReg, mips_ram_1_p6
  MainControl maincontrol_1 (
    .op5(ins[31]), .op4(ins[30]), .op3(ins[29]), .op2(ins[28]), .op1(ins[27]), .op0(ins[26]),
    .RegDst(RegDst), .ALUSrc(ALUSrc), .MemtoReg(MemtoReg), .RegWrite(RegWr), .MemWrite(MemWr),
    .nPC_sel(nPC_sel), .Jump(Jump), .ExtOp(ExtOp), .ALUop2(ALUop2), .ALUop1(ALUop1), .ALUop0(ALUop0));
  Multiplexer #(.width(32), .enable("false")) multiplexer_6 (
    .in0(multiplexer_5_out), .in1({JumpPC, ins[25:16], Imm16, 2'b00}), .out(npc), .sel(Jump));
  // MIPSProgramROM mipsprogramrom_1: pin names not known; wires that end beside it: {JumpPC, pc}, {ins, Imm16}
  Multiplexer #(.width(32), .enable("false")) multiplexer_7 (
    .in0(mips_alu_1_p4), .in1(mips_ram_1_p6), .out(registerfile_1_p1), .sel(MemtoReg));

  // Other names for the same wires on the sheet: ins[15:0] = Imm16; JumpPC[27:2] = {ins[25:16], Imm16};
  //   Rd[4:0] = Imm16[15:11]; Rt[4:0] = ins[20:16]; Rs[4:0] = ins[25:21]; pc[31:28] = JumpPC

  // Notes on the sheet:
  //   Fetch
  //   Decode
  //   Execute&Memory
  //   Control Path
  //   PC
  //   Simulation controll pannel
  //   contents of mipsprogramrom_1 (hex, n*v repeats v):
  //   loop: addiu $t5,$zero,9 addiu $t6,$zero,9 addu $t7,$t5,$t6 subu $t8,$t5,$t6
  //   #以上测试了addu,addiu,subu指令 addiu $s0,$zero,0   #将地址为最开始的基址放入$s0 addiu $t1,$zero,10 addiu $t2,$zero,0
  //   addiu $t3,$zero,100 ori $t2,$t2,1       #测试ori指令 beq $zero,$zero,condition  #测试beq指令 addiu
  //   $t5,$zero,0 j ocondition         condition: sw $t2,0($s0)    #测试sw指令 lw $t3,0($s0)    #测试lw指令
  //   ocondition: addiu $t4,$zero,9 subu $t1,$t1,$t4 sw $t1,4($s0) lw $t4,4($s0) j loop
  //   #测试Jump指令，之后会一直循环执行
endmodule

module MainControl (
  input  op5,
  input  op4,
  input  op3,
  input  op2,
  input  op1,
  input  op0,
  output RegDst,
  output ALUSrc,
  output MemtoReg,
  output RegWrite,
  output MemWrite,
  output nPC_sel,
  output Jump,
  output ExtOp,
  output ALUop2,
  output ALUop1,
  output ALUop0
);

  wire and_1_out, and_2_out, and_3_out, and_4_out, and_5_out, and_6_out, and_7_out, and_12_out, and_13_out,
       not_2_out, not_3_out, not_4_out, not_5_out, not_6_out, not_7_out, not_8_out, not_9_out, not_10_out,
       not_11_out, not_12_out, not_14_out, not_15_out, not_16_out, not_17_out, not_18_out, not_19_out,
       not_20_out, not_21_out;

  not not_1 (RegDst, op0);
  not not_2 (not_2_out, op2);
  and and_1 (and_1_out, not_2_out, not_3_out);
  not not_3 (not_3_out, op1);
  and and_2 (and_2_out, op3, not_4_out);
  not not_4 (not_4_out, op1);
  and and_3 (and_3_out, op5, not_5_out);
  not not_5 (not_5_out, op3);
  and and_4 (and_4_out, op3, not_6_out, not_7_out);
  not not_6 (not_6_out, op2);
  not not_7 (not_7_out, op0);
  not not_8 (not_8_out, op2);
  and and_5 (and_5_out, op3, not_8_out, op1);
  and and_6 (and_6_out, op4, op3, not_9_out);
  not not_9 (not_9_out, op2);
  and and_7 (and_7_out, op5, op3, not_10_out);
  not not_10 (not_10_out, op2);
  not not_11 (not_11_out, op3);
  and and_8 (nPC_sel, not_11_out, op2);
  and and_9 (Jump, op1, not_12_out);
  not not_12 (not_12_out, op0);
  not not_13 (ExtOp, op2);
  not not_14 (not_14_out, op2);
  and and_10 (ALUop2, not_14_out, not_15_out);
  not not_15 (not_15_out, op1);
  and and_11 (ALUop1, op3, not_16_out);
  not not_16 (not_16_out, op1);
  not not_17 (not_17_out, op3);
  not not_18 (not_18_out, op5);
  not not_19 (not_19_out, op4);
  not not_20 (not_20_out, op2);
  not not_21 (not_21_out, op1);
  or or_1 (RegWrite, and_1_out, and_2_out, and_3_out);
  or or_2 (MemWrite, and_4_out, and_5_out, and_6_out, and_7_out);
  and and_12 (and_12_out, not_17_out, op2);
  and and_13 (and_13_out, not_18_out, not_19_out, op3, not_20_out, not_21_out, op0);
  or or_3 (ALUop0, and_12_out, and_13_out);

  assign ALUSrc = op0;
  assign MemtoReg = op1;
endmodule

module ALUControl (
  input  ALUop2,
  input  ALUop1,
  input  ALUop0,
  input  func3,
  input  func2,
  input  func1,
  input  func0,
  output ALUctr3,
  output ALUctr2,
  output ALUctr1,
  output ALUctr0
);

  wire and_1_out, and_2_out, and_3_out, and_4_out, and_5_out, and_6_out, not_1_out, not_2_out, not_3_out,
       not_4_out, not_5_out, not_6_out, not_7_out, not_8_out, not_9_out;

  not not_1 (not_1_out, ALUop2);
  not not_2 (not_2_out, ALUop0);
  not not_3 (not_3_out, ALUop1);
  not not_4 (not_4_out, ALUop0);
  not not_5 (not_5_out, ALUop2);
  not not_6 (not_6_out, ALUop1);
  not not_7 (not_7_out, ALUop0);
  not not_8 (not_8_out, func3);
  not not_9 (not_9_out, func2);
  and and_1 (and_1_out, not_1_out, ALUop1);
  and and_2 (and_2_out, ALUop1, not_2_out);
  and and_3 (and_3_out, not_3_out, ALUop0);
  and and_4 (and_4_out, ALUop2, not_4_out, func1);
  or or_1 (ALUctr1, not_5_out, not_6_out, ALUop0);
  and and_5 (and_5_out, ALUop2, not_7_out, not_8_out, not_9_out, func0);
  and and_6 (and_6_out, ALUop2, ALUop1);
  or or_2 (ALUctr3, and_1_out, and_2_out);
  or or_3 (ALUctr2, and_3_out, and_4_out);
  or or_4 (ALUctr0, and_5_out, and_6_out);
endmodule
